# Fritzing sketch Schema_Progetto (saved by Fritzing 0.8.7b)
breadboards: 1

parts:
  U2 = 74HC595 [package="DIP16 [THT]"]
  U3 = 7-SEGMENT-DISPLAY-1_-RED [package=7-segment-1_pth]  # not connected
  Componente1 = Arduino Uno (Rev3)

nets:
  VCC: U2.MR, U2.VCC, Componente1.5V
  N1: U2.OE, Componente1.VIN
  N2: U2.DS, Componente1.D4
